# Fritzing sketch UV_light_circuit (saved by Fritzing 0.8.7b)
breadboards: 1

parts:
  ferrite_core_transformer = Transformer [part_number=1 package=transformer]
  R1 = Resistor [package="2512 [SMD]"]
  VCC1 = Battery

nets:
  N1: ferrite_core_transformer.1, R1.Pin_1
  N2: ferrite_core_transformer.5, R1.Pin_0, VCC1.+

custom parts:
  Transformer: Small transformers (Ferrite Core)
