# Fritzing sketch power&brain_circuit (saved by Fritzing 0.8.7b)
breadboards: 1

parts:
  U1 = Voltage Regulator - 5V [package="DPak [SMD]"]
  U2 = Voltage Regulator - 5V [package="DPak [SMD]"]
  U3 = Voltage Regulator - 5V [package="DPak [SMD]"]
  JP1 = Header 2 [package=screwterminal-3.5mm-2_lock]
  Part1 = SRF05 Ultrasonic Rangefinder
  Part2 = SRF05 Ultrasonic Rangefinder
  Part3 = SRF05 Ultrasonic Rangefinder
  Part4 = SRF05 Ultrasonic Rangefinder
  Part5 = SRF05 Ultrasonic Rangefinder
  R1 = Resistor [tolerance=±5% resistance=220 package=THT]
  LED2 = LED - 3mm [color="Red (633nm)" package="3 mm [THT]"]
  IR1 = TSOP312.., 314.. [package=THT]
  IR2 = TSOP312.., 314.. [package=THT]
  U4 = SWITCH-SPST-2 [package=switch-spst-vertical]
  Q1 = NPN-Transistor [package="TO92 [THT]"]
  U5 = USB_AB [package=usb-ab-micro-smd]
  IC1 = MICROCONTROLLER [package=dil28-3-simon]
  U6 = SWITCH-SPST-2 [package=switch-spst-vertical]
  Raspberry_Pi_Zero1 = Raspberry Pi Zero
  S1 = H-Bridge with L298N
  M1 = DC Motor
  M2 = DC Motor
  82ohms = Resistor [package="2010 [SMD]"]
  R2 = Resistor [tolerance=±5% resistance=220 package=THT]
  R3 = Resistor [tolerance=±5% resistance=220 package=THT]
  R4 = Resistor [tolerance=±5% resistance=220 package=THT]
  R5 = Resistor [tolerance=±5% resistance=220 package=THT]

nets:
  N1: U1.input_voltage, U2.input_voltage, U3.input_voltage, JP1.1, S1.12V, R5.Pin_0
  GND: U1.GND, U2.GND, U3.GND, Part1.GND, Part2.GND, Part3.GND, Part4.GND, Part5.GND, R1.Pin_0, IR1.GND, IR2.GND, U4.P, Q1.E, U5.GND, S1.GND, R2.Pin_1
  N2: U1.output_voltage, U6.P
  VCC: U2.output_voltage, Part1.VCC, Part2.VCC, Part3.VCC, Part4.VCC, Part5.VCC, LED2.anode, IR1.Vs, IR2.Vs, IC1.VCC
  N3: JP1.2, U4.O
  N4: Part1.Trig, Raspberry_Pi_Zero1.GIPO9
  N5: Part1.Echo, Raspberry_Pi_Zero1.GIPO11
  N6: Part2.Trig, Raspberry_Pi_Zero1.GPIO2
  N7: Part2.Echo, Raspberry_Pi_Zero1.GPIO3
  N8: Part3.Trig, Raspberry_Pi_Zero1.GIPO4
  N9: Part3.Echo, Raspberry_Pi_Zero1.GIPO17
  N10: Part4.Trig, Raspberry_Pi_Zero1.GIPO27
  N11: Part4.Echo, Raspberry_Pi_Zero1.GIPO22
  N12: Part5.Trig, Raspberry_Pi_Zero1.GIPO23
  N13: Part5.Echo, Raspberry_Pi_Zero1.GIPO24
  N14: IR1.Data, IC1.PC4(ADC4_SDA)
  N15: IR2.Data, IC1.PC5(ADC5_SCL)
  N16: Q1.B, 82ohms.Pin_0
  N17: Q1.C, IC1.GND
  N18: U5.VBUS, U6.O
  N19: IC1.PD0(RXD), Raspberry_Pi_Zero1.GIPO14
  N20: IC1.PD1(TXD), Raspberry_Pi_Zero1.GIPO15
  N21: IC1.PC3(ADC3), R3.Pin_1, R4.Pin_0
  N22: Raspberry_Pi_Zero1.GIPO10, 82ohms.Pin_1
  N23: Raspberry_Pi_Zero1.GIPO21, S1.IN1
  N24: Raspberry_Pi_Zero1.GIPO20, S1.IN2
  N25: Raspberry_Pi_Zero1.GIPO16, S1.IN3
  N26: Raspberry_Pi_Zero1.GIPO12, S1.IN4
  N27: Raspberry_Pi_Zero1.GIPO7, S1.ENA
  N28: Raspberry_Pi_Zero1.GIPO8, S1.ENB
  N29: S1.M1-01, M1.pin_1
  N30: S1.M1-02, M1.pin_2
  N31: S1.M2-01, M2.pin_2
  N32: S1.M2-02, M2.pin_1
  N33: R2.Pin_0, R3.Pin_0
  N34: R4.Pin_1, R5.Pin_1

notes:
  USB connector
  powers Raspberry pi zero w via usb cable
  Screw_terminal
  Connects with 11.1V 3300mAh LIPO Battery
  R1
  IR1,IR2 TSOP 1738
  npn transistor 2N2222A
  Sonar 1-5
  HC-SR04
  ATMega328p
  Raspberry Pi zero w
  7805 voltage regulator
  R2
  R1 - 82ohms
  R2 - 220ohms
  L1 - 3mm red LED
  R3 to R6 - 10k ohms(for battery charging level)
  L1
  l298N Motor Driver
  S1,S2
  SPST toggle switch
  R3-R6

custom parts:
  H-Bridge with L298N: h-bridge
